# Fritzing sketch Elevator_circuit (saved by Fritzing 0.9.3b)
breadboards: 1

parts:
  Part1 = Arduino Uno (Rev3)
  LED_Våning_1 = LED - 5mm [color="Red (633nm)" package="5 mm [THT]"]
  R1 = Resistor [tolerance=±5% resistance=1k package=THT]
  HissKnappVåning_1 = Pushbutton [package="[THT]"]
  HissKnappVåning_2 = Pushbutton [package="[THT]"]
  LED_Våning_2 = LED - 5mm [color="Red (633nm)" package="5 mm [THT]"]
  R2 = Resistor [tolerance=±5% resistance=1k package=THT]
  HissKnappVåning_3 = Pushbutton [package="[THT]"]
  LED_Våning_3 = LED - 5mm [color="Red (633nm)" package="5 mm [THT]"]
  R3 = Resistor [tolerance=±5% resistance=1k package=THT]
  R4 = Resistor [tolerance=±5% resistance=10k package=THT]
  R5 = Resistor [tolerance=±5% resistance=10k package=THT]
  R6 = Resistor [tolerance=±5% resistance=10k package=THT]

nets:
  N1: Part1.D8, LED_Våning_3.anode
  N2: Part1.D9_PWM, LED_Våning_2.anode
  N3: Part1.D10_PWM/SS, LED_Våning_1.anode
  N4: Part1.GND, R1.Pin_1, HissKnappVåning_1.Pin_2, HissKnappVåning_2.Pin_1, HissKnappVåning_2.Pin_2, R2.Pin_1, HissKnappVåning_3.Pin_1, HissKnappVåning_3.Pin_2, R3.Pin_1
  N5: Part1.D0/RX, HissKnappVåning_1.Pin_3, HissKnappVåning_1.Pin_4, R4.Pin_1
  N6: Part1.D1/TX, HissKnappVåning_2.Pin_3, HissKnappVåning_2.Pin_4, R5.Pin_1
  N7: Part1.D2, HissKnappVåning_3.Pin_3, HissKnappVåning_3.Pin_4, R6.Pin_1
  N8: Part1.5V, R4.Pin_0, R5.Pin_0, R6.Pin_0
  N9: LED_Våning_1.cathode, R1.Pin_0
  N10: LED_Våning_2.cathode, R2.Pin_0
  N11: LED_Våning_3.cathode, R3.Pin_0
